# Fritzing sketch cirucuito modulo wifi (saved by Fritzing 0.9.1b)
circuit board: 8.46667cm x 5.64444cm
breadboards: 1

parts:
  Parte1 = Arduino Uno (Rev3)
  ESP8266 = ESP8266

nets:
  GND: Parte1.GND, ESP8266.GND
  N1: Parte1.D2, ESP8266.UTXD
  N2: Parte1.D3_PWM, ESP8266.URXD
  3V3: Parte1.3V3, ESP8266.CH_PD, ESP8266.VCC

// code stored in the sketch: modulo_wifi.ino
#include <SoftwareSerial.h>
SoftwareSerial wifiPort(2,3); // RX, TX
void setup()
{
  Serial.begin(9600);
  wifiPort.begin(9600);
  wifiPort.println("AT+RST");
  delay(1000);
  wifiPort.println("AT");
}
void loop() // run over and over
{
  wifiPort.listen();
  if (wifiPort.available() ) {
    Serial.write(wifiPort.read());
  }
  if (Serial.available() ){
    wifiPort.write(Serial.read());
  }
}
